# Fritzing sketch wiring (saved by Fritzing 0.9.1b)
breadboards: 1

parts:
  S1 = Pushbutton [package="[THT]"]
  パーツ1 = Arduino Uno (Rev3)
  LED1 = LED - 5mm [color="Blue (470nm)" package="5 mm [THT]"]
  LED2 = LED - 5mm [color="White (4500K)" package="5 mm [THT]"]
  LED3 = LED - 5mm [color="Green (565nm)" package="5 mm [THT]"]
  LED4 = LED - 5mm [color="Yellow (595nm)" package="5 mm [THT]"]
  S2 = Pushbutton [package="[THT]"]
  S3 = Pushbutton [package="[THT]"]
  S4 = Pushbutton [package="[THT]"]

nets:
  N1: S1.Pin_1, S1.Pin_2, パーツ1.D7
  N2: S1.Pin_3, S1.Pin_4, パーツ1.GND, LED1.cathode, LED2.cathode, LED3.cathode, LED4.cathode, S2.Pin_3, S2.Pin_4, S3.Pin_3, S3.Pin_4, S4.Pin_3, S4.Pin_4
  N3: パーツ1.D9_PWM, LED4.anode
  N4: パーツ1.D10_PWM/SS, LED1.anode
  N5: パーツ1.D11_PWM/MOSI, LED2.anode
  N6: パーツ1.D12/MISO, LED3.anode
  N7: パーツ1.D4, S4.Pin_1, S4.Pin_2
  N8: パーツ1.D5_PWM, S3.Pin_1, S3.Pin_2
  N9: パーツ1.D6_PWM, S2.Pin_1, S2.Pin_2
