# Fritzing sketch wiring (saved by Fritzing 0.9.1b)
breadboards: 1

parts:
  パーツ1 = Arduino Uno (Rev3)
  RE1 = Rotary Encoder [package=THT]
  LED1 = LED - 5mm [color="Red (633nm)" package="5 mm [THT]"]

nets:
  N1: パーツ1.A0, RE1.EncoderPinC
  N2: パーツ1.D11_PWM/MOSI, LED1.anode
  N3: パーツ1.GND, RE1.EncoderPinA, LED1.cathode
  N4: パーツ1.5V, RE1.EncoderPinB
