# Fritzing sketch wiring (saved by Fritzing 0.9.2b)
breadboards: 1

parts:
  LED1 = RGB LED (com. cathode, rgb) [package="5 mm [THT]"]
  パーツ1 = Arduino Uno (Rev3)
  C1 = Ceramic Capacitor [capacitance=100nF package="100 mil [THT, multilayer]"]
  R1 = Resistor [tolerance=±5% resistance=220 package=THT]

nets:
  N1: LED1.common_cathode, パーツ1.GND, C1.0
  N2: LED1.green_anode, C1.1, R1.Pin_0
  N3: LED1.blue_anode, パーツ1.D2
  N4: パーツ1.5V, R1.Pin_1
