# Fritzing sketch dht11 (saved by Fritzing 0.9.2b)
breadboards: 1

parts:
  パーツ1 = Arduino Uno (Rev3)
  DHT1 = DHT11 Humitidy and Temperature Sensor
  R1 = Resistor [tolerance=±5% resistance=1k package=THT]

nets:
  N1: パーツ1.D2, DHT1.DATA, R1.Pin_1
  5V: パーツ1.5V, DHT1.VDD, R1.Pin_0

custom parts:
  DHT11 Humitidy and Temperature Sensor: DHT11 Humidity and Temperature Sensor
