# Fritzing sketch 2 (saved by Fritzing 0.9.1b)
breadboards: 1

parts:
  S1 = Pushbutton [package="[THT]"]
  パーツ1 = Arduino Uno (Rev3)
  J1 = Piezo Speaker

nets:
  N1: S1.Pin_1, S1.Pin_2, パーツ1.D10_PWM/SS
  N2: S1.Pin_3, S1.Pin_4, パーツ1.GND, J1.pin1
  N3: パーツ1.D11_PWM/MOSI, J1.pin2

notes:
  このスピーカーは、どっちにさしても大丈夫
