# Fritzing sketch doremi (saved by Fritzing 0.9.1b)
breadboards: 1

parts:
  J1 = Piezo Speaker
  パーツ1 = Arduino Uno (Rev3)

nets:
  N1: J1.pin1, パーツ1.GND
  N2: J1.pin2, パーツ1.D12/MISO

notes:
  スピーカーは、どっちにさしても大丈夫です
