# Fritzing sketch doremi_buttons (saved by Fritzing 0.9.1b)
breadboards: 1

parts:
  J1 = Piezo Speaker
  パーツ1 = Arduino Uno (Rev3)
  S1 = Pushbutton [package="[THT]"]
  S2 = Pushbutton [package="[THT]"]
  S3 = Pushbutton [package="[THT]"]

nets:
  N1: J1.pin1, パーツ1.GND, S1.Pin_3, S1.Pin_4, S2.Pin_3, S2.Pin_4, S3.Pin_3, S3.Pin_4
  N2: J1.pin2, パーツ1.D12/MISO
  N3: パーツ1.D4, S3.Pin_1, S3.Pin_2
  N4: パーツ1.D5_PWM, S2.Pin_1, S2.Pin_2
  N5: パーツ1.D6_PWM, S1.Pin_1, S1.Pin_2

notes:
  スピーカーは、どっちにさしても大丈夫です
