# Fritzing sketch dotmatrix (saved by Fritzing 0.9.2b)
breadboards: 2

parts:
  パーツ1 = Arduino Uno (Rev3)
  Disp1 = LBT2088AH [part_number=LBT2088AH]
  R1 = Resistor [tolerance=±5% resistance=1k package=THT]
  R2 = Resistor [tolerance=±5% resistance=1k package=THT]
  R3 = Resistor [tolerance=±5% resistance=1k package=THT]
  R4 = Resistor [tolerance=±5% resistance=1k package=THT]
  R5 = Resistor [tolerance=±5% resistance=1k package=THT]
  R6 = Resistor [tolerance=±5% resistance=1k package=THT]
  R7 = Resistor [tolerance=±5% resistance=1k package=THT]
  R8 = Resistor [tolerance=±5% resistance=1k package=THT]

nets:
  N1: パーツ1.A0, Disp1.pin_11
  N2: パーツ1.A1, Disp1.pin_15
  N3: パーツ1.A2, Disp1.pin_16
  N4: パーツ1.D8, Disp1.pin_13
  N5: パーツ1.D9_PWM, Disp1.pin_3
  N6: パーツ1.D10_PWM/SS, Disp1.pin_4
  N7: パーツ1.D11_PWM/MOSI, Disp1.pin_10
  N8: パーツ1.D12/MISO, Disp1.pin_6
  N9: パーツ1.D0/RX, R3.Pin_1
  N10: パーツ1.D1/TX, R1.Pin_1
  N11: パーツ1.D2, R8.Pin_0
  N12: パーツ1.D3_PWM, R2.Pin_1
  N13: パーツ1.D4, R4.Pin_0
  N14: パーツ1.D5_PWM, R7.Pin_0
  N15: パーツ1.D6_PWM, R5.Pin_0
  N16: パーツ1.D7, R6.Pin_0
  N17: Disp1.pin1, R4.Pin_1
  N18: Disp1.pin2, R5.Pin_1
  N19: Disp1.pin_5, R6.Pin_1
  N20: Disp1.pin_7, R7.Pin_1
  N21: Disp1.pin_8, R8.Pin_1
  N22: Disp1.pin_9, R3.Pin_0
  N23: Disp1.pin_12, R2.Pin_0
  N24: Disp1.pin_14, R1.Pin_0
