# Fritzing sketch lcd (saved by Fritzing 0.9.1b)

parts:
  パーツ1 = Arduino Uno (Rev3)
  GLCD_128x1 = 128 x 64 Graphic LCD

nets:
  N1: パーツ1.D8, GLCD_128x1.4_D/I
  N2: パーツ1.D9_PWM, GLCD_128x1.6_Enable
  N3: パーツ1.D4, GLCD_128x1.11_DB4
  N4: パーツ1.D5_PWM, GLCD_128x1.12_DB5
  N5: パーツ1.D6_PWM, GLCD_128x1.13_DB6
  N6: パーツ1.D7, GLCD_128x1.14_DB7
  N7: パーツ1.5V, GLCD_128x1.1_Vss
  N8: パーツ1.GND, GLCD_128x1.2_Vdd

notes:
  せつぞく
  rs:8
  enable:9
  D4:4
  D5:5
  D6:6
  D7:7
