# Fritzing sketch led_button (saved by Fritzing 0.9.1b)
breadboards: 1

parts:
  S1 = Pushbutton [package="[THT]"]
  パーツ1 = Arduino Uno (Rev3)
  LED1 = LED - 5mm [color="Red (633nm)" package="5 mm [THT]"]

nets:
  N1: S1.Pin_1, S1.Pin_2, パーツ1.D10_PWM/SS
  N2: S1.Pin_3, S1.Pin_4, パーツ1.GND, LED1.cathode
  N3: パーツ1.D11_PWM/MOSI, LED1.anode
