# Fritzing sketch led_optical (saved by Fritzing 0.9.1b)
breadboards: 2

parts:
  パーツ1 = Arduino Uno (Rev3)
  R1 = Photocell (LDR) [package=THT]
  RE1 = Rotary Encoder [package=THT]
  LED1 = LED - 5mm [color="Red (633nm)" package="5 mm [THT]"]

nets:
  N1: パーツ1.A0, R1.pin_0, RE1.EncoderPinB
  N2: パーツ1.D11_PWM/MOSI, LED1.anode
  N3: パーツ1.GND, RE1.EncoderPinA, LED1.cathode
  N4: パーツ1.5V, R1.pin_1

notes:
  固定抵抗のかわりに使いました。
