# Fritzing sketch rgbled2 (saved by Fritzing 0.9.2b)
breadboards: 1

parts:
  LED1 = RGB LED (com. cathode, rgb) [package="5 mm [THT]"]
  パーツ1 = Arduino Uno (Rev3)
  C1 = Ceramic Capacitor [capacitance=100nF package="100 mil [THT, multilayer]"]
  R1 = Resistor [tolerance=±5% resistance=1k package=THT]
  LED2 = RGB LED (com. cathode, rgb) [package="5 mm [THT]"]
  C2 = Ceramic Capacitor [capacitance=100nF package="100 mil [THT, multilayer]"]
  R2 = Resistor [tolerance=±5% resistance=1k package=THT]

nets:
  N1: LED1.red_anode, LED2.blue_anode
  N2: LED1.common_cathode, パーツ1.GND, C1.0, LED2.common_cathode, C2.0
  N3: LED1.green_anode, C1.1, R1.Pin_0
  N4: LED1.blue_anode, パーツ1.D2
  N5: パーツ1.5V, R1.Pin_1, R2.Pin_1
  N6: LED2.green_anode, C2.1, R2.Pin_0
