# Fritzing sketch dcmotor (saved by Fritzing 0.9.1b)

parts:
  パーツ1 = Arduino Uno (Rev3)
  M1 = DC Motor
  M2 = DC Motor

nets:
  N1: パーツ1.D2, M2.pin_2
  N2: パーツ1.D3_PWM, M2.pin_1
  N3: パーツ1.D4, M1.pin_2
  N4: パーツ1.D5_PWM, M1.pin_1

notes:
  モーターへの接続はイメージです。
  途中の配線は省略しています。
