# Fritzing sketch 2 (saved by Fritzing 0.9.2b)
breadboards: 1

parts:
  パーツ1 = Arduino Uno (Rev3)
  J1 = Piezo Speaker
  パーツ2 = Parallax 2-Axis Joystick
  LED1 = LED - 5mm [color="Red (633nm)" package="5 mm [THT]"]

nets:
  N1: パーツ1.A0, パーツ2.L/R_Out
  N2: パーツ1.A1, パーツ2.U/D_Out
  N3: パーツ1.D11_PWM/MOSI, LED1.anode
  N4: パーツ1.D12/MISO, J1.pin2
  GND: パーツ1.GND, J1.pin1, パーツ2.GND, LED1.cathode
  N5: パーツ1.5V, パーツ2.L/R_Vcc, パーツ2.U/D_Vcc

custom parts:
  Parallax 2-Axis Joystick: Description: This is the Parallax 2-Axis Joystick. It contains a spring return thumb joystick mounted to a breakout board. The breakout board breaks out the joysticks connections to .1" pin headers. The joystick's connections are duplicated on both sides of the board for easy use. This part can easily be used on a breadboard due to the .1" pin headers, but can also be soldered into any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
