# Fritzing sketch 1 (saved by Fritzing 0.9.1b)
breadboards: 1

parts:
  パーツ1 = HC-SR04 Ultrasonic Rangemeter
  パーツ2 = Arduino Uno (Rev3)

nets:
  VCC: パーツ1.VCC, パーツ2.5V
  N1: パーツ1.Trig, パーツ2.D9_PWM, パーツ2.D7
  N2: パーツ1.Echo, パーツ2.D8
  GND: パーツ1.GND, パーツ2.GND
